// Logisim project Project pt3 with counter.circ as structural Verilog: 1 circuit, main circuit main
module main (
  output D,
  output out_2,
  output out_3,
  output out_4,
  output [3:0] out_5
);

  wire and_1_out, and_2_out, and_3_out, and_4_out, clock_1_out, decoder_1_out0, decoder_1_out1,
       decoder_1_out2, decoder_1_out3, decoder_1_out4, decoder_1_out5, decoder_1_out6, decoder_1_out7,
       decoder_1_out8, decoder_1_out9, or_1_out, or_2_out, or_3_out, or_4_out, or_5_out, or_6_out, or_7_out,
       or_8_out, t_ff_1_qn, undriven, undriven_2;

  Decoder #(.select(4)) decoder_1 (
    .out0(decoder_1_out0), .out1(decoder_1_out1), .out2(decoder_1_out2), .out3(decoder_1_out3),
    .out4(decoder_1_out4), .out5(decoder_1_out5), .out6(decoder_1_out6), .out7(decoder_1_out7),
    .out8(decoder_1_out8), .out9(decoder_1_out9), .sel({D, out_2, out_3, out_4}));  // open: out10, out11, out12, out13, out14, out15, en
  or or_1 (or_1_out, decoder_1_out1, decoder_1_out2, decoder_1_out4, decoder_1_out5, decoder_1_out7, decoder_1_out9);
  or or_2 (or_2_out, decoder_1_out0, decoder_1_out1, decoder_1_out2, decoder_1_out3, decoder_1_out4, decoder_1_out5, decoder_1_out6, decoder_1_out7, decoder_1_out8, decoder_1_out9);
  or or_3 (or_3_out, decoder_1_out0, decoder_1_out1, decoder_1_out2, decoder_1_out3, decoder_1_out4, decoder_1_out5, decoder_1_out6, decoder_1_out7, decoder_1_out8);
  or or_4 (or_4_out, decoder_1_out1, decoder_1_out2, decoder_1_out4, decoder_1_out5, decoder_1_out7, decoder_1_out9);
  or or_5 (or_5_out, decoder_1_out4, decoder_1_out5, decoder_1_out7, decoder_1_out9);
  or or_6 (or_6_out, decoder_1_out1, decoder_1_out4, decoder_1_out5, decoder_1_out6, decoder_1_out7, decoder_1_out8);
  or or_7 (or_7_out, decoder_1_out1, decoder_1_out2, decoder_1_out4, decoder_1_out6, decoder_1_out8, decoder_1_out9);
  _7_Segment_Display u_7_segment_display_1 (
    .g(or_7_out), .f(or_6_out), .a(or_1_out), .b(or_2_out), .e(or_5_out), .d(or_4_out), .c(or_3_out),
    .dp(undriven));
  Clock clock_1 (.out(clock_1_out));
  and and_1 (and_1_out, out_4, out_3, out_2);
  and and_2 (and_2_out, out_4, D);
  or or_8 (or_8_out, and_1_out, and_2_out);
  and and_3 (and_3_out, out_3, out_4);
  and and_4 (and_4_out, t_ff_1_qn, out_4);
  T_Flip_Flop t_ff_1 (.clk(clock_1_out), .T(or_8_out), .Q(D), .Qn(t_ff_1_qn));  // open: preset, reset, en
  T_Flip_Flop t_ff_2 (.clk(clock_1_out), .T(and_3_out), .Q(out_2));  // open: Qn, preset, reset, en
  T_Flip_Flop t_ff_3 (.clk(clock_1_out), .T(and_4_out), .Q(out_3));  // open: Qn, preset, reset, en
  T_Flip_Flop t_ff_4 (.clk(clock_1_out), .T(1'b1), .Q(out_4), .preset(undriven_2));  // open: Qn, reset, en

  assign out_5 = {D, out_2, out_3, out_4};

  // Notes on the sheet:
  //   4X16
  //   a
  //   b
  //   c
  //   d
  //   e
  //   f
  //   g
  //   a
  //   f
  //   g
  //   d
  //   e
  //   b
  //   dot
  //   c
  //   2
  //   3
  //   4
  //   5
  //   6
  //   7
  //   8
  //   9
  //   0
  //   1
  //   1931804042
  //   DECODER
  //   Parinda Rahman 
  //   D
  //   D'
  //   C
  //   C'
  //   B
  //   B'
  //   A
  //   A'
  //   A
  //   C
  //   B
endmodule
